# Fritzing sketch Wiring diagram (saved by Fritzing 0.9.4)
breadboards: 1

parts:
  ZS-042_RTC1 = ZS-042 RTC Module
  LED1 = LED - 5mm [color="Red (633nm)" package="5 mm [THT]"]
  R1 = Resistor [tolerance=±5% resistance=220 package=THT]
  SG2 = Buzzer 12mm [package=buzzer-12mm-ns]
  GND = single row smd female pin header, 1 pin [form="♀ (female)"]
  3v3 = female pin header, 1 pin [form="♀ (female)"]
  P10 = female pin header, 1 pin [form="♀ (female)"]
  P19 = female pin header, 1 pin [form="♀ (female)"]
  SCL = female pin header, 1 pin [form="♀ (female)"]
  SDA = female pin header, 1 pin [form="♀ (female)"]

nets:
  N1: ZS-042_RTC1.GND, R1.Pin_1, SG2.1, GND.pin1
  N2: ZS-042_RTC1.VCC, 3v3.pin1
  N3: ZS-042_RTC1.SDA, SDA.pin1
  N4: ZS-042_RTC1.SCL, SCL.pin1
  N5: LED1.cathode, R1.Pin_0
  N6: LED1.anode, P10.pin1
  N7: SG2.2, P19.pin1
